# Fritzing sketch PongGame-V1.1 (saved by Fritzing 0.9.3b)
breadboards: 1

parts:
  Parça1 = Arduino Uno (Rev3) - ICSP
  Parça2 = Bluetooth HC-05 Macho
  8x8_LED_Modul_mit_MAX1 = 8x8 LED Modul mit MAX7219 [package=THT]
  J1 = Piezo Speaker
  LED1 = LED - 3mm [color="Red (633nm)" package="3 mm [THT]"]
  R1 = Resistor [tolerance=±5% resistance=220 package="0805 [SMD]"]
  R2 = Resistor [tolerance=±5% resistance=220 package="0805 [SMD]"]

nets:
  5V: Parça1.5V, Parça2.VCC, 8x8_LED_Modul_mit_MAX1.VCC_Eingang
  N1: Parça1.D8, R2.Pin_1
  N2: Parça1.D9_PWM, R1.Pin_1
  N3: Parça1.D10_PWM/SS, 8x8_LED_Modul_mit_MAX1.CS_Eingang
  N4: Parça1.D11_PWM/MOSI, 8x8_LED_Modul_mit_MAX1.CLK_Eingang
  N5: Parça1.D12/MISO, 8x8_LED_Modul_mit_MAX1.DIN_Eingang
  N6: Parça1.D0/RX, Parça2.TXD
  N7: Parça1.D1/TX, Parça2.RXD
  GND: Parça1.GND, Parça2.GND, 8x8_LED_Modul_mit_MAX1.GND_Eingang, J1.pin1, LED1.cathode
  N8: J1.pin2, R2.Pin_0
  N9: LED1.anode, R1.Pin_0
